// Digital circuit Main.dig as structural Verilog
module Main (
  input  in_1,
  input  in_2,
  input  in_3,
  input  in_4,
  input  in_5,
  input  in_6,
  input  in_7,
  input  in_8,
  input  in_9,
  input  in_10,
  input  in_11,
  input  in_12,
  input  [7:0] in_13,
  input  in_14,
  input  in_15
);

  wire ABus;
  wire [7:0] _8balu_1_p8, _74574_2_p20, DataBus, multiplexer_1_out, stackaddressgen_1_address;

  // _74161 _74161_1: pin names not known
  // _74574 _74574_1: pin names not known; wires that end beside it: DataBus[0], DataBus[1], DataBus[2], DataBus[3], DataBus[4], DataBus[5], DataBus[6], DataBus[7], 1'b1, 1'b0
  // PC pc_1: pin names not known; wires that end beside it: ABus
  Multiplexer #(.Bits(8)) multiplexer_1 (.sel(in_6), .in_0(_8balu_1_p8), .in_1(DataBus), .out(multiplexer_1_out));
  StackAddressGen stackaddressgen_1 (
    .Down(in_3), .Up(in_4), .CLR(in_5), .Address(stackaddressgen_1_address));  // open: nUnderflow, nOverflow
  // _74574 _74574_2: pin names not known; wires that end beside it: 1'b0, in_7, multiplexer_1_out[0], multiplexer_1_out[1], multiplexer_1_out[2], multiplexer_1_out[3], multiplexer_1_out[4], multiplexer_1_out[5], multiplexer_1_out[6], multiplexer_1_out[7], 1'b1, 1'b0, _74574_2_p20[0], _74574_2_p20[1], _74574_2_p20[2], _74574_2_p20[3], _74574_2_p20[4], _74574_2_p20[5], _74574_2_p20[6], _74574_2_p20[7]
  // _74138 _74138_1: pin names not known
  assign DataBus = in_15 ? _74574_2_p20 : 8'bz;  // Driver driver_1
  RAMSinglePortSel #(.AddrBits(8), .Bits(8)) ramsingleportsel_1 (
    .A(stackaddressgen_1_address), .CS(1'b1), .WE(in_1), .OE(in_2), .D(DataBus));
  // _8bALU _8balu_1: pin names not known; wires that end beside it: _74574_2_p20, DataBus, in_8, in_9, in_10, in_11, in_12, _8balu_1_p8
  assign DataBus = in_14 ? in_13 : 8'bz;  // Driver driver_2
  PullDown #(.Bits(8)) pulldown_1 (.out(DataBus));
endmodule
