// Digital circuit PC.dig as structural Verilog
module PC (
  input  [7:0] DataBus,
  input  CountUp,
  input  nCLR,
  input  CLK,
  input  nLD_Low,
  input  nLD_High,
  output [15:0] Address
);

  wire _74161_1_p12, _74161_2_p12, _74161_3_p12;

  // _74161 _74161_1: pin names not known; wires that end beside it: nLD_Low, nCLR, CLK, 1'b1, CountUp, DataBus[0], DataBus[1], DataBus[2], DataBus[3], 1'b1, 1'b0, _74161_1_p12, Address[0], Address[1], Address[2], Address[3]
  // _74161 _74161_2: pin names not known; wires that end beside it: nLD_Low, nCLR, CLK, _74161_1_p12, CountUp, DataBus[4], DataBus[5], DataBus[6], DataBus[7], 1'b1, 1'b0, _74161_2_p12, Address[4], Address[5], Address[6], Address[7]
  // _74161 _74161_3: pin names not known; wires that end beside it: nLD_High, nCLR, CLK, _74161_2_p12, CountUp, DataBus[0], DataBus[1], DataBus[2], DataBus[3], 1'b1, 1'b0, _74161_3_p12, Address[8], Address[9], Address[10], Address[11]
  // _74161 _74161_4: pin names not known; wires that end beside it: nLD_High, nCLR, CLK, _74161_3_p12, CountUp, DataBus[4], DataBus[5], DataBus[6], DataBus[7], 1'b1, 1'b0, Address[12], Address[13], Address[14], Address[15]

  // Other names for the same wires on the sheet: Enable = CountUp; nLD = nLD_Low; nLDH = nLD_High
endmodule
